# Fritzing sketch circuito (saved by Fritzing 0.9.3b)
breadboards: 1

parts:
  R1 = Resistor [tolerance=±5% resistance=220 package=THT]
  R2 = Resistor [tolerance=±5% resistance=220 package=THT]
  Componente1 = Arduino Nano (Rev3.0)
  LED1 = LED - 5mm [color="Red (633nm)" package="5 mm [THT]"]
  LED2 = LED - 5mm [color="Red (660nm)" package="5 mm [THT]"]
  U1 = ESP8266 WiFi Module [part_number=ESP8266]
  R3 = Resistor [tolerance=±5% resistance=1k package=THT]
  Q1 = NPN-Transistor [package="TO92 [THT]"]
  SG2 = Buzzer 12mm [package=buzzer-ccv-kit]
  R4 = Resistor [tolerance=±5% resistance=220 package=THT]
  LED3 = LED - 5mm [color="Red (660nm)" package="5 mm [THT]"]
  RELAY1 = CAR RELAY [part_number=NVF4-2 package=THT]
  Componente2 = RFID-RC522-v2
  R5 = Photocell (LDR) [package=THT]
  S1 = Round Pushbutton
  L1 = Inductor [package="400 mil [THT]"]
  R6 = Resistor [tolerance=±20% resistance=10k package=THT]
  R7 = Resistor [tolerance=±5% resistance=10k package=THT]
  S2 = Reed switch [package=THT]
  R8 = Resistor [tolerance=±10% resistance=10k package=THT]

nets:
  N1: R1.Pin_0, Componente1.D6
  N2: R1.Pin_1, LED2.anode
  N3: R2.Pin_0, Componente1.D7
  N4: R2.Pin_1, LED1.anode
  GND/GND PIR: Componente1.GND, LED1.cathode, LED2.cathode, U1.GND, Q1.E, SG2.2, LED3.cathode, Componente2.GND, L1.pin_1, R6.Pin_0, R7.Pin_0, R8.Pin_0
  N5: Componente1.D2, U1.TXD
  N6: Componente1.D3, U1.RXD
  N7: Componente1.D4, R3.Pin_0
  N8: Componente1.D5, SG2.1
  N9: Componente1.D8, R4.Pin_0
  N10: Componente1.D9, Componente2.RST
  N11: Componente1.D10, Componente2.SDA
  N12: Componente1.D11/MOSI, Componente2.MOSI
  N13: Componente1.D12/MISO, Componente2.MISO
  5V/VCC PIR: Componente1.5V, R5.pin_1, S1.leg1, S2.pin_1
  N14: Componente1.A3, S2.pin_2, R8.Pin_1
  N15: Componente1.A2, S1.leg0, R7.Pin_1
  TLL PIR: Componente1.A1
  N16: Componente1.A0, R5.pin_0, R6.Pin_1
  N17: Componente1.D13/SCK, Componente2.SCK
  3.3V: U1.VCC, U1.RST, Componente2.3.3V
  N18: R3.Pin_1, Q1.B
  N19: Q1.C, RELAY1.86
  N20: R4.Pin_1, LED3.anode
  12V: RELAY1.85, RELAY1.87
  N21: RELAY1.30, L1.pin_0

custom parts:
  ESP8266 WiFi Module: Generic WiFi Module based on the ESP8266 with onboard PCB antenna and UART communications
  RFID-RC522-v2: A simple China made RFID-RC522 Reader; do check the pin labels, as this is a MFRC522 based clone.
